# Fritzing sketch YalerCampFire (saved by Fritzing 0.7.11b)
breadboards: 1

parts:
  Arduino_Ethernet_Shield1 = Arduino Ethernet Shield
  red_LED = LED - 5mm [color="Red (633nm)" package="5 mm [THT]"]
  R1_(220_Ohm) = Resistor [tolerance=±5% resistance=220 package=THT]
  yellow_LED = LED - 5mm [color="Red (633nm)" package="5 mm [THT]"]
  R2_(220_Ohm) = Resistor [tolerance=±5% resistance=220 package=THT]

nets:
  N1: Arduino_Ethernet_Shield1.D6, yellow_LED.cathode
  N2: Arduino_Ethernet_Shield1.D3, red_LED.cathode
  N3: Arduino_Ethernet_Shield1.+5V, R1_(220_Ohm).Pin_0, R2_(220_Ohm).Pin_0
  N4: red_LED.anode, R2_(220_Ohm).Pin_1
  N5: R1_(220_Ohm).Pin_1, yellow_LED.anode
